# Fritzing sketch forkliftElectronics (saved by Fritzing 0.8.5b)

parts:
  Part1 = Arduino Pro Mini v13
  U1 = TRANSCHIPTC5747 [package=camera_sfv24r-2st_2]  # not connected
  U2 = BATTERY-2 [package=battery-aaa]
  U3 = BATTERY-2 [package=battery-aaa]
  U4 = BATTERY-2 [package=battery-aaa]
  U5 = BATTERY-2 [package=battery-aaa]
  JP1 = Header 5x2 [package=2x5-ra]
  U6 = mystery part, 8 pins [chip_label="Forklift PCB"]
  J1 = Screw terminal - 2 pins [package=THT]
  Part3 = Ambient Light Sensor (TEMT6000 Breakout Board)
  Part4 = Ambient Light Sensor (TEMT6000 Breakout Board)
  Part5 = Ambient Light Sensor (TEMT6000 Breakout Board)  # not connected
  Part6 = Ambient Light Sensor (TEMT6000 Breakout Board)  # not connected
  J2 = Screw terminal - 2 pins [package=THT]

nets:
  N1: Part1.RAW, U5.-1, U6.pin1, J2.pin1
  VCC: Part1.VCC, J1.pin2, Part3.VCC, Part4.VCC
  N2: Part1.A3, JP1.7
  N3: Part1.A2, JP1.8
  N4: Part1.A1, JP1.9
  N5: Part1.A0, JP1.10
  N6: Part1.D11_PWM/MOSI, JP1.6, U6.pin3
  N7: Part1.D10_PWM/SS, JP1.5, U6.pin4
  N8: Part1.D8, JP1.1, U6.pin6
  N9: Part1.D6_PWM, JP1.3, U6.pin5
  GND: Part1.GND, U6.pin2, J1.pin1, Part3.GND, Part4.GND, J2.pin2
  N10: U2.-1, U3.+1
  N11: U3.-1, U4.+1
  N12: U4.-1, U5.+1

notes:
  Forklift PCB GND->VCC = 4.6V
